# Fritzing sketch midi_hold (saved by Fritzing 0.9.3b)
breadboards: 1

parts:
  Part1 = Arduino Nano (Rev3.0) (ICSP)
  R1 = Resistor [tolerance=±5% resistance=220 package="0805 [SMD]"]
  Grove1 = Grove 4 Digit Display
  RE2 = KY-040 Rotary encoder [package=THT]
  RE1 = KY-040 Rotary encoder [package=THT]
  DIN1 = DIN-5 jack (MIDI) [package=THT]  # not connected

nets:
  N1: Part1.D1/TX, R1.Pin_0, R1.Pin_1
  GND: Part1.GND, Grove1.GND, RE2.GND, RE1.GND
  N2: Part1.D2, Grove1.CLK
  N3: Part1.D3, Grove1.DIO
  N4: Part1.D4, RE1.CLK
  N5: Part1.D5, RE1.DT
  N6: Part1.D6, RE1.SW
  N7: Part1.D7, RE2.CLK
  N8: Part1.D8, RE2.DT
  N9: Part1.D9, RE2.SW
  VCC: Part1.5V, Grove1.VCC, RE2.Vcc, RE1.Vcc

custom parts:
  KY-040 Rotary encoder: KY-040 Rotary Encoder with switch on breakout borad from AZ Delivery
